# Fritzing sketch scheme (saved by Fritzing 0.9.10b)
breadboards: 1

parts:
  LCM1602_IIC2 = LCM1602 IIC [part_number="LCM1602 IIC" chip_label="LCM1602 IIC" package="DIP (Dual Inline) [THT]"]
  LCD1 = LCD screen
  Part1 = Arduino Mega 2560 (Rev3)
  Keypad4x1 = Keypad Membran 4x4

nets:
  VSS: LCM1602_IIC2.VSS, LCD1.VSS
  VDD: LCM1602_IIC2.VDD, LCD1.VDD
  N1: LCM1602_IIC2.V0, LCD1.V0
  N2: LCM1602_IIC2.RS, LCD1.RS
  N3: LCM1602_IIC2.RW, LCD1.R/W
  N4: LCM1602_IIC2.E, LCD1.E
  N5: LCM1602_IIC2.D0, LCD1.DB0
  N6: LCM1602_IIC2.D1, LCD1.DB1
  N7: LCM1602_IIC2.D2, LCD1.DB2
  N8: LCM1602_IIC2.D3, LCD1.DB3
  N9: LCM1602_IIC2.D4, LCD1.DB4
  N10: LCM1602_IIC2.D5, LCD1.DB5
  N11: LCM1602_IIC2.D6, LCD1.DB6
  N12: LCM1602_IIC2.D7, LCD1.DB7
  N13: LCM1602_IIC2.A, LCD1.LED+
  N14: LCM1602_IIC2.K, LCD1.LED-
  GND: LCM1602_IIC2.GND, Part1.GND
  VCC: LCM1602_IIC2.VCC, Part1.5V
  N15: LCM1602_IIC2.SDA, Part1.D20/SDA
  N16: LCM1602_IIC2.SCL, Part1.D21/SCL
  N17: Part1.D9_PWM, Keypad4x1.Pin1
  N18: Part1.D8_PWM, Keypad4x1.Pin2
  N19: Part1.D2_PWM, Keypad4x1.Pin8
  N20: Part1.D3_PWM, Keypad4x1.Pin7
  N21: Part1.D4_PWM, Keypad4x1.Pin6
  N22: Part1.D5_PWM, Keypad4x1.Pin5
  N23: Part1.D6_PWM, Keypad4x1.Pin4
  N24: Part1.D7_PWM, Keypad4x1.Pin3

custom parts:
  LCM1602 IIC: I2C-Module to use a 1602 or 2004 LCD on with the wire.h libory Serial LCD Modul
  Keypad Membran 4x4: Membrane Keypad 4x4 Matrix
